// Logisim project trabCD.circ as structural Verilog: 1 circuit, main circuit main
module main (
  input  [1:0] in_1,
  input  [5:0] in_2,
  input  [1:0] in_3,
  input  in_4,
  input  [1:0] in_5
);

  wire [1:0] bitselector_1_out, bitselector_2_out, bitselector_3_out;
  wire [5:0] rom_1_data;

  ROM #(.addrWidth(6), .dataWidth(6)) rom_1 (.addr(in_2), .data(rom_1_data), .sel(in_4));
  BitSelector #(.width(6), .group(2)) bitselector_1 (.in(rom_1_data), .out(bitselector_1_out), .sel(in_1));
  BitSelector #(.width(6), .group(2)) bitselector_2 (.in(rom_1_data), .out(bitselector_2_out), .sel(in_3));
  BitSelector #(.width(6), .group(2)) bitselector_3 (.in(rom_1_data), .out(bitselector_3_out), .sel(in_5));
  DotMatrix #(.inputtype("row"), .matrixcols(2), .matrixrows(3), .dotshape("circle")) dotmatrix_1 (
    .row0(bitselector_1_out), .row1(bitselector_2_out), .row2(bitselector_3_out));

  // Notes on the sheet:
  //   contents of rom_1 (hex, n*v repeats v):
  //   14 21 21 3 13 21 21 3 21 21 33 3f 21 32 13 31
endmodule
